// Logisim project 2107086_ALU.circ as structural Verilog: 8 circuits, main circuit main
module main (
  input  C1,
  input  C2,
  input  [17:0] A,
  input  [17:0] B,
  output [17:0] newresult,
  output is_it_negative_87be2e7e,
  output zero,
  output Overflow,
  output Sign,
  output Carry
);

  wire resultzero_1_allzero;
  wire [17:0] _18_Bit_Adder_result, _18_Bit_AND_out_3, _18_Bit_OR_out_3, multiplexer_1_out;

  AND _18_Bit_AND (.in_1(A), .in_2(B), .out_3(_18_Bit_AND_out_3));
  OR _18_Bit_OR (.in_1(A), .in_2(B), .out_3(_18_Bit_OR_out_3));
  overflow_check _18_Bit_Adder (
    .B(A), .A(B), .Mode(C1), .Carry(Carry), .Sign(Sign), .Overflow(Overflow), .Result(_18_Bit_Adder_result));
  Multiplexer #(.width(18)) multiplexer_1 (
    .in0(_18_Bit_AND_out_3), .in1(_18_Bit_OR_out_3), .out(multiplexer_1_out), .sel(C1));
  Multiplexer #(.width(18)) multiplexer_2 (
    .in0(multiplexer_1_out), .in1(_18_Bit_Adder_result), .out(newresult), .sel(C2));
  L_16h_7388e337 l_16h_7388e337_1 (.result(newresult), .signcheck_isnegative_a6271365(is_it_negative_87be2e7e));
  resultzero resultzero_1 (.result1(newresult), .allzero(resultzero_1_allzero));
  not not_1 (zero, resultzero_1_allzero);

  // Notes on the sheet:
  //   2107086_ALU
  //   A 2nd operand
  //   B 1st operand
  //   00=AND
  //   01=ADD
  //   10=OR
  //   11=SUB
endmodule

module Adder_1Bit (
  input  Cin,
  input  A,
  input  B,
  output Sum,
  output Carry
);

  wire and_1_out, and_2_out, xor_1_out;

  xor xor_1 (xor_1_out, A, B);
  and and_1 (and_1_out, A, B);
  xor xor_2 (Sum, Cin, xor_1_out);
  and and_2 (and_2_out, Cin, xor_1_out);
  or or_1 (Carry, and_1_out, and_2_out);
endmodule

module complement (
  input  Mode,
  input  [17:0] Input,
  output [17:0] out_3
);

  xor xor_1 (out_3[0], Mode, Input[0]);
  xor xor_2 (out_3[1], Mode, Input[1]);
  xor xor_3 (out_3[2], Mode, Input[2]);
  xor xor_4 (out_3[3], Mode, Input[3]);
  xor xor_5 (out_3[4], Mode, Input[4]);
  xor xor_6 (out_3[5], Mode, Input[5]);
  xor xor_7 (out_3[6], Mode, Input[6]);
  xor xor_8 (out_3[7], Mode, Input[7]);
  xor xor_9 (out_3[8], Mode, Input[8]);
  xor xor_10 (out_3[9], Mode, Input[9]);
  xor xor_11 (out_3[10], Mode, Input[10]);
  xor xor_12 (out_3[11], Mode, Input[11]);
  xor xor_13 (out_3[12], Mode, Input[12]);
  xor xor_14 (out_3[13], Mode, Input[13]);
  xor xor_15 (out_3[14], Mode, Input[14]);
  xor xor_16 (out_3[15], Mode, Input[15]);
  xor xor_17 (out_3[16], Mode, Input[16]);
  xor xor_18 (out_3[17], Mode, Input[17]);
endmodule

module overflow_check (
  input  Mode,
  input  [17:0] B,
  input  [17:0] A,
  output [17:0] Result,
  output Sign,
  output Overflow,
  output Carry
);

  wire adder_1bit_1_carry, adder_1bit_2_carry, adder_1bit_3_carry, adder_1bit_4_carry, adder_1bit_5_carry,
       adder_1bit_6_carry, adder_1bit_7_carry, adder_1bit_8_carry, adder_1bit_9_carry, adder_1bit_10_carry,
       adder_1bit_11_carry, adder_1bit_12_carry, adder_1bit_13_carry, adder_1bit_14_carry,
       adder_1bit_15_carry, adder_1bit_16_carry, adder_1bit_17_carry, and_1_out, and_2_out, not_1_out,
       not_2_out, not_3_out;
  wire [17:0] complement_1_out_3;

  complement complement_1 (.Input(B), .Mode(Mode), .out_3(complement_1_out_3));
  Adder_1Bit adder_1bit_1 (
    .A(A[0]), .B(complement_1_out_3[0]), .Cin(Mode), .Carry(adder_1bit_1_carry), .Sum(Result[0]));
  Adder_1Bit adder_1bit_2 (
    .A(A[1]), .B(complement_1_out_3[1]), .Cin(adder_1bit_1_carry), .Carry(adder_1bit_2_carry), .Sum(Result[1]));
  Adder_1Bit adder_1bit_3 (
    .A(A[2]), .B(complement_1_out_3[2]), .Cin(adder_1bit_2_carry), .Carry(adder_1bit_3_carry), .Sum(Result[2]));
  Adder_1Bit adder_1bit_4 (
    .A(A[3]), .B(complement_1_out_3[3]), .Cin(adder_1bit_3_carry), .Carry(adder_1bit_4_carry), .Sum(Result[3]));
  Adder_1Bit adder_1bit_5 (
    .A(A[4]), .B(complement_1_out_3[4]), .Cin(adder_1bit_4_carry), .Carry(adder_1bit_5_carry), .Sum(Result[4]));
  Adder_1Bit adder_1bit_6 (
    .A(A[5]), .B(complement_1_out_3[5]), .Cin(adder_1bit_5_carry), .Carry(adder_1bit_6_carry), .Sum(Result[5]));
  Adder_1Bit adder_1bit_7 (
    .A(A[6]), .B(complement_1_out_3[6]), .Cin(adder_1bit_6_carry), .Carry(adder_1bit_7_carry), .Sum(Result[6]));
  Adder_1Bit adder_1bit_8 (
    .A(A[7]), .B(complement_1_out_3[7]), .Cin(adder_1bit_7_carry), .Carry(adder_1bit_8_carry), .Sum(Result[7]));
  Adder_1Bit adder_1bit_9 (
    .A(A[8]), .B(complement_1_out_3[8]), .Cin(adder_1bit_8_carry), .Carry(adder_1bit_9_carry), .Sum(Result[8]));
  Adder_1Bit adder_1bit_10 (
    .A(A[9]), .B(complement_1_out_3[9]), .Cin(adder_1bit_9_carry), .Carry(adder_1bit_10_carry),
    .Sum(Result[9]));
  Adder_1Bit adder_1bit_11 (
    .A(A[10]), .B(complement_1_out_3[10]), .Cin(adder_1bit_10_carry), .Carry(adder_1bit_11_carry),
    .Sum(Result[10]));
  Adder_1Bit adder_1bit_12 (
    .A(A[11]), .B(complement_1_out_3[11]), .Cin(adder_1bit_11_carry), .Carry(adder_1bit_12_carry),
    .Sum(Result[11]));
  Adder_1Bit adder_1bit_13 (
    .A(A[12]), .B(complement_1_out_3[12]), .Cin(adder_1bit_12_carry), .Carry(adder_1bit_13_carry),
    .Sum(Result[12]));
  Adder_1Bit adder_1bit_14 (
    .A(A[13]), .B(complement_1_out_3[13]), .Cin(adder_1bit_13_carry), .Carry(adder_1bit_14_carry),
    .Sum(Result[13]));
  Adder_1Bit adder_1bit_15 (
    .A(A[14]), .B(complement_1_out_3[14]), .Cin(adder_1bit_14_carry), .Carry(adder_1bit_15_carry),
    .Sum(Result[14]));
  Adder_1Bit adder_1bit_16 (
    .A(A[15]), .B(complement_1_out_3[15]), .Cin(adder_1bit_15_carry), .Carry(adder_1bit_16_carry),
    .Sum(Result[15]));
  Adder_1Bit adder_1bit_17 (
    .A(A[16]), .B(complement_1_out_3[16]), .Cin(adder_1bit_16_carry), .Carry(adder_1bit_17_carry),
    .Sum(Result[16]));
  Adder_1Bit adder_1bit_18 (
    .A(A[17]), .B(complement_1_out_3[17]), .Cin(adder_1bit_17_carry), .Carry(Carry), .Sum(Result[17]));
  not not_1 (not_1_out, A[17]);
  not not_2 (not_2_out, complement_1_out_3[17]);
  not not_3 (not_3_out, Result[17]);
  and and_1 (and_1_out, Result[17], not_2_out, not_1_out);
  and and_2 (and_2_out, complement_1_out_3[17], not_3_out, A[17]);
  or or_1 (Overflow, and_1_out, and_2_out);

  assign Sign = Result[17];
endmodule

module AND (
  input  [17:0] in_1,
  input  [17:0] in_2,
  output [17:0] out_3
);

  and and_1 (out_3[0], in_1[0], in_2[0]);
  and and_2 (out_3[1], in_1[1], in_2[1]);
  and and_3 (out_3[2], in_1[2], in_2[2]);
  and and_4 (out_3[3], in_1[3], in_2[3]);
  and and_5 (out_3[4], in_1[4], in_2[4]);
  and and_6 (out_3[5], in_1[5], in_2[5]);
  and and_7 (out_3[6], in_1[6], in_2[6]);
  and and_8 (out_3[7], in_1[7], in_2[7]);
  and and_9 (out_3[8], in_1[8], in_2[8]);
  and and_10 (out_3[9], in_1[9], in_2[9]);
  and and_11 (out_3[10], in_1[10], in_2[10]);
  and and_12 (out_3[11], in_1[11], in_2[11]);
  and and_13 (out_3[12], in_1[12], in_2[12]);
  and and_14 (out_3[13], in_1[13], in_2[13]);
  and and_15 (out_3[14], in_1[14], in_2[14]);
  and and_16 (out_3[15], in_1[15], in_2[15]);
  and and_17 (out_3[16], in_1[16], in_2[16]);
  and and_18 (out_3[17], in_1[17], in_2[17]);
endmodule

module OR (
  input  [17:0] in_1,
  input  [17:0] in_2,
  output [17:0] out_3
);

  or or_1 (out_3[0], in_1[0], in_2[0]);
  or or_2 (out_3[1], in_1[1], in_2[1]);
  or or_3 (out_3[2], in_1[2], in_2[2]);
  or or_4 (out_3[3], in_1[3], in_2[3]);
  or or_5 (out_3[4], in_1[4], in_2[4]);
  or or_6 (out_3[5], in_1[5], in_2[5]);
  or or_7 (out_3[6], in_1[6], in_2[6]);
  or or_8 (out_3[7], in_1[7], in_2[7]);
  or or_9 (out_3[8], in_1[8], in_2[8]);
  or or_10 (out_3[9], in_1[9], in_2[9]);
  or or_11 (out_3[10], in_1[10], in_2[10]);
  or or_12 (out_3[11], in_1[11], in_2[11]);
  or or_13 (out_3[12], in_1[12], in_2[12]);
  or or_14 (out_3[13], in_1[13], in_2[13]);
  or or_15 (out_3[14], in_1[14], in_2[14]);
  or or_16 (out_3[15], in_1[15], in_2[15]);
  or or_17 (out_3[16], in_1[16], in_2[16]);
  or or_18 (out_3[17], in_1[17], in_2[17]);
endmodule

module L_16h_7388e337 (
  input  [17:0] result,
  output signcheck_isnegative_a6271365
);


  assign signcheck_isnegative_a6271365 = result[17];
endmodule

module resultzero (
  input  [17:0] result1,
  output allzero
);

  or or_1 (allzero, result1[0], result1[1], result1[2], result1[3], result1[4], result1[5], result1[6], result1[7], result1[8], result1[9], result1[10], result1[11], result1[12], result1[13], result1[14], result1[15], result1[16], result1[17]);
endmodule
