// Logisim project 2107086_cpu.circ as structural Verilog: 9 circuits, main circuit main
module main (
  input  Control_0,
  input  Control_1,
  input  Control_2,
  input  [17:0] A,
  input  [17:0] B,
  output [17:0] Result,
  output Zero,
  output Negative,
  output Carry,
  output Overflow
);

  wire [17:0] l_18_bit_and_bf9cda56_1_result, l_18_bit_not_39575eab_1_result, l_18_bit_or_8cfa111d_1_result,
       l_18_bit_xor_9205e3ca_1_result, l_18bitadder_6bea6f73_1_result, multiplexer_1_out, multiplexer_2_out,
       multiplexer_3_out;

  L_18_bit_xor_9205e3ca l_18_bit_xor_9205e3ca_1 (.A(A), .B(B), .Result(l_18_bit_xor_9205e3ca_1_result));
  L_18_bit_not_39575eab l_18_bit_not_39575eab_1 (.A(A), .Result(l_18_bit_not_39575eab_1_result));
  L_18_bit_AND_bf9cda56 l_18_bit_and_bf9cda56_1 (.A(A), .B(B), .Result(l_18_bit_and_bf9cda56_1_result));
  L_18_bit_OR_8cfa111d l_18_bit_or_8cfa111d_1 (.A(A), .B(B), .Result(l_18_bit_or_8cfa111d_1_result));
  Multiplexer #(.width(18)) multiplexer_1 (
    .in0(l_18_bit_xor_9205e3ca_1_result), .in1(l_18_bit_not_39575eab_1_result), .out(multiplexer_1_out),
    .sel(Control_1));
  L_18bitadder_6bea6f73 l_18bitadder_6bea6f73_1 (
    .B(B), .A(A), .Mode(Control_0), .Carry(Carry), .Overflow(Overflow),
    .Result(l_18bitadder_6bea6f73_1_result));  // open: Sign
  Multiplexer #(.width(18)) multiplexer_2 (
    .in0(l_18_bit_and_bf9cda56_1_result), .in1(l_18_bit_or_8cfa111d_1_result), .out(multiplexer_2_out),
    .sel(Control_0));
  Multiplexer #(.width(18)) multiplexer_3 (
    .in0(multiplexer_2_out), .in1(l_18bitadder_6bea6f73_1_result), .out(multiplexer_3_out), .sel(Control_1));
  Multiplexer #(.width(18)) multiplexer_4 (
    .in0(multiplexer_3_out), .in1(multiplexer_1_out), .out(Result), .sel(Control_2));
  zero_negative zero_negative_1 (.A(Result), .Zero(Zero), .Negative(Negative));
endmodule

// AND
module L_18_bit_AND_bf9cda56 (
  input  [17:0] A,
  input  [17:0] B,
  output [17:0] Result
);

  assign Result = A & B;  // AND_Gate and_1, 18 bits wide
endmodule

// OR
module L_18_bit_OR_8cfa111d (
  input  [17:0] A,
  input  [17:0] B,
  output [17:0] Result
);

  assign Result = A | B;  // OR_Gate or_1, 18 bits wide
endmodule

module L_1_bit_adder_b58cd21c (
  input  A,
  input  B,
  input  Cin,
  output S,
  output Cout
);

  wire and_1_out, and_2_out, xor_1_out;

  xor xor_1 (xor_1_out, A, B);
  and and_1 (and_1_out, xor_1_out, Cin);
  and and_2 (and_2_out, B, A);
  xor xor_2 (S, xor_1_out, Cin);
  or or_1 (Cout, and_1_out, and_2_out);
endmodule

// +/-
module L_18_bit_adder_subtractor_23074777 (
  input  Control,
  input  [17:0] A,
  input  [17:0] B,
  output [17:0] Result,
  output Carry,
  output Overflow
);

  wire [17:0] bit_extender_1_out, xor_1_out;

  assign bit_extender_1_out = {{17{Control}}, Control};  // Bit_Extender bit_extender_1
  assign xor_1_out = bit_extender_1_out ^ B;  // XOR_Gate xor_1, 18 bits wide
  L_18bitadder_6bea6f73 l_18bitadder_6bea6f73_1 (
    .B(xor_1_out), .A(A), .Mode(Control), .Carry(Carry), .Overflow(Overflow), .Result(Result));  // open: Sign
endmodule

module zero_negative (
  input  [17:0] A,
  output Zero,
  output Negative
);

  nor nor_1 (Zero, A[0], A[1], A[2], A[3], A[4], A[5], A[6], A[7], A[8], A[10], A[11], A[12], A[13], A[14], A[15], A[16], A[9], A[17]);

  assign Negative = A[17];
endmodule

// XOR
module L_18_bit_xor_9205e3ca (
  input  [17:0] A,
  input  [17:0] B,
  output [17:0] Result
);

  assign Result = A ^ B;  // XOR_Gate xor_1, 18 bits wide
endmodule

// NOT
module L_18_bit_not_39575eab (
  input  [17:0] A,
  output [17:0] Result
);

  assign Result = ~A;  // NOT_Gate not_1, 18 bits wide
endmodule

module L_18bitadder_6bea6f73 (
  input  Mode,
  input  [17:0] B,
  input  [17:0] A,
  output [17:0] Result,
  output Sign,
  output Overflow,
  output Carry
);

  wire adder_1bit_1_p4, adder_1bit_2_p4, adder_1bit_3_p4, adder_1bit_4_p4, adder_1bit_5_p4, adder_1bit_6_p4,
       adder_1bit_7_p4, adder_1bit_8_p4, adder_1bit_9_p4, adder_1bit_10_p5, adder_1bit_11_p4,
       adder_1bit_12_p4, adder_1bit_13_p4, adder_1bit_14_p4, adder_1bit_15_p4, adder_1bit_16_p4,
       adder_1bit_17_p4, and_1_out, and_2_out, not_1_out, not_2_out, not_3_out;
  wire [17:0] complement_1_p3;

  // complement complement_1: pin names not known; wires that end beside it: B, Mode, complement_1_p3
  // Adder_1Bit adder_1bit_1: pin names not known; wires that end beside it: A[0], complement_1_p3[0], Mode, adder_1bit_1_p4, Result[0]
  // Adder_1Bit adder_1bit_2: pin names not known; wires that end beside it: A[1], complement_1_p3[1], adder_1bit_1_p4, adder_1bit_2_p4, Result[1]
  // Adder_1Bit adder_1bit_3: pin names not known; wires that end beside it: A[2], complement_1_p3[2], adder_1bit_2_p4, adder_1bit_3_p4, Result[2]
  // Adder_1Bit adder_1bit_4: pin names not known; wires that end beside it: A[3], complement_1_p3[3], adder_1bit_3_p4, adder_1bit_4_p4, Result[3]
  // Adder_1Bit adder_1bit_5: pin names not known; wires that end beside it: A[4], complement_1_p3[4], adder_1bit_4_p4, adder_1bit_5_p4, Result[4]
  // Adder_1Bit adder_1bit_6: pin names not known; wires that end beside it: A[5], complement_1_p3[5], adder_1bit_5_p4, adder_1bit_6_p4, Result[5]
  // Adder_1Bit adder_1bit_7: pin names not known; wires that end beside it: A[6], complement_1_p3[6], adder_1bit_6_p4, adder_1bit_7_p4, Result[6]
  // Adder_1Bit adder_1bit_8: pin names not known; wires that end beside it: A[7], complement_1_p3[7], adder_1bit_7_p4, adder_1bit_8_p4, Result[7]
  // Adder_1Bit adder_1bit_9: pin names not known; wires that end beside it: A[8], complement_1_p3[8], adder_1bit_8_p4, adder_1bit_9_p4, Result[8]
  // Adder_1Bit adder_1bit_10: pin names not known; wires that end beside it: complement_1_p3[9], A[9], complement_1_p3[9], adder_1bit_9_p4, adder_1bit_10_p5, Result[9]
  // Adder_1Bit adder_1bit_11: pin names not known; wires that end beside it: A[10], complement_1_p3[10], adder_1bit_10_p5, adder_1bit_11_p4, Result[10]
  // Adder_1Bit adder_1bit_12: pin names not known; wires that end beside it: A[11], complement_1_p3[11], adder_1bit_11_p4, adder_1bit_12_p4, Result[11]
  // Adder_1Bit adder_1bit_13: pin names not known; wires that end beside it: A[12], complement_1_p3[12], adder_1bit_12_p4, adder_1bit_13_p4, Result[12]
  // Adder_1Bit adder_1bit_14: pin names not known; wires that end beside it: A[13], complement_1_p3[13], adder_1bit_13_p4, adder_1bit_14_p4, Result[13]
  // Adder_1Bit adder_1bit_15: pin names not known; wires that end beside it: A[14], complement_1_p3[14], adder_1bit_14_p4, adder_1bit_15_p4, Result[14]
  // Adder_1Bit adder_1bit_16: pin names not known; wires that end beside it: A[15], complement_1_p3[15], adder_1bit_15_p4, adder_1bit_16_p4, Result[15]
  // Adder_1Bit adder_1bit_17: pin names not known; wires that end beside it: A[16], complement_1_p3[16], adder_1bit_16_p4, adder_1bit_17_p4, Result[16]
  // Adder_1Bit adder_1bit_18: pin names not known; wires that end beside it: A[17], complement_1_p3[17], adder_1bit_17_p4, Carry, Result[17]
  not not_1 (not_1_out, A[17]);
  not not_2 (not_2_out, complement_1_p3[17]);
  not not_3 (not_3_out, Result[17]);
  and and_1 (and_1_out, Result[17], not_2_out, not_1_out);
  and and_2 (and_2_out, complement_1_p3[17], not_3_out, A[17]);
  or or_1 (Overflow, and_1_out, and_2_out);

  assign Sign = Result[17];
endmodule
